// Logisim project BIN2DEC.circ as structural Verilog: 1 circuit, main circuit main
module main (
  input  [7:0] in_1,
  output [3:0] out_2,
  output [3:0] out_3,
  output [3:0] out_4
);

  wire and_1_out, and_2_out, and_3_out, and_12_out, and_13_out, and_14_out, and_15_out, and_16_out,
       and_17_out, and_18_out, and_19_out, and_20_out, and_21_out, and_22_out, and_23_out, and_24_out,
       and_25_out, and_26_out, and_27_out, and_28_out, and_29_out, and_30_out, and_31_out, and_32_out,
       and_33_out, and_34_out, and_35_out, and_36_out, and_37_out, and_38_out, and_39_out, and_40_out,
       and_41_out, and_42_out, and_43_out, and_44_out, and_45_out, and_46_out, and_47_out, and_48_out,
       and_67_out, and_68_out, and_69_out, and_70_out, and_71_out, and_72_out, and_73_out, and_74_out,
       and_75_out, and_76_out, and_77_out, and_78_out, and_79_out, and_80_out, and_81_out, and_82_out,
       and_83_out, and_84_out, and_85_out, and_86_out, and_87_out, and_88_out, and_89_out, and_90_out,
       not_1_out, not_2_out, not_3_out, not_4_out, not_5_out, not_6_out, not_7_out, not_8_out, not_9_out,
       not_10_out, not_11_out, not_12_out, not_13_out, not_14_out, not_15_out, not_16_out, not_17_out,
       or_1_out, or_2_out, or_3_out, or_6_out, or_7_out, or_8_out, or_9_out, or_10_out, or_11_out, or_12_out,
       or_13_out, or_14_out, or_15_out, or_16_out, or_17_out, or_18_out, or_19_out, or_20_out, or_21_out,
       or_22_out, or_23_out, or_24_out, or_25_out, or_26_out, or_27_out, or_28_out, or_29_out, or_30_out,
       or_33_out, or_34_out, or_35_out, or_36_out, or_37_out, or_38_out, or_39_out, or_40_out, xor_1_out,
       xor_2_out, xor_3_out, xor_4_out, xor_5_out, xor_6_out, xor_7_out, xor_8_out, xor_9_out, xor_10_out,
       xor_11_out, xor_12_out, xor_13_out, xor_14_out, xor_15_out, xor_16_out, xor_34_out, xor_35_out,
       xor_36_out, xor_37_out, xor_38_out, xor_39_out, xor_40_out, xor_41_out, xor_42_out, xor_43_out,
       xor_44_out, xor_45_out, xor_46_out, xor_47_out, xor_48_out, xor_49_out;
  wire [1:0] and_5_out;
  wire [3:0] and_6_out, and_7_out, and_8_out, and_49_out, and_50_out, and_52_out, and_53_out, and_54_out,
       and_59_out, and_60_out, and_61_out, and_66_out, xor_54_out;
  wire [3:3] nor_1_out, xor_25_out, xor_26_out, xor_27_out, xor_28_out, xor_29_out, xor_30_out, xor_31_out,
       xor_32_out;
  wire [7:0] and_9_out, and_10_out, and_11_out, and_51_out, and_55_out, and_56_out, and_57_out, and_58_out,
       and_62_out, and_63_out, and_64_out, and_65_out, or_5_out, or_32_out, xor_17_out;
  wire [7:7] xor_33_out;

  or or_1 (or_1_out, in_1[2], in_1[3], in_1[4]);
  and and_1 (and_1_out, in_1[5], in_1[6]);
  or or_2 (or_2_out, in_1[3], in_1[4], in_1[5]);
  and and_2 (and_2_out, in_1[6], in_1[7]);
  and and_3 (and_3_out, or_1_out, and_1_out);
  and and_4 (and_5_out[1], or_2_out, and_2_out);
  or or_3 (or_3_out, and_3_out, in_1[7]);
  not not_1 (not_1_out, and_5_out[1]);
  and and_5 (and_5_out[0], or_3_out, not_1_out);
  nor nor_1 (nor_1_out[3], and_5_out[0], and_5_out[1]);
  assign and_6_out = {4{nor_1_out[3]}} & 4'b0000;  // AND_Gate and_6, 4 bits wide
  assign and_7_out = {4{and_5_out[0]}} & 4'b0001;  // AND_Gate and_7, 4 bits wide
  assign and_8_out = {4{and_5_out[1]}} & 4'b0010;  // AND_Gate and_8, 4 bits wide
  assign out_4 = and_6_out | and_7_out | and_8_out;  // OR_Gate or_4, 4 bits wide
  assign and_9_out = {8{1'b0}} & {8{nor_1_out[3]}};  // AND_Gate and_9, 8 bits wide
  assign and_10_out = 8'h64 & {8{and_5_out[0]}};  // AND_Gate and_10, 8 bits wide
  assign and_11_out = 8'hc8 & {8{and_5_out[1]}};  // AND_Gate and_11, 8 bits wide
  assign or_5_out = and_9_out | and_10_out | and_11_out;  // OR_Gate or_5, 8 bits wide
  not not_2 (not_2_out, or_5_out[7]);
  not not_3 (not_3_out, or_5_out[4]);
  not not_4 (not_4_out, or_5_out[5]);
  not not_5 (not_5_out, or_5_out[6]);
  not not_6 (not_6_out, or_5_out[2]);
  not not_7 (not_7_out, or_5_out[3]);
  not not_8 (not_8_out, or_5_out[0]);
  not not_9 (not_9_out, or_5_out[1]);
  xor xor_1 (xor_1_out, 1'b1, not_8_out);
  and and_12 (and_12_out, 1'b1, not_8_out);
  xor xor_2 (xor_2_out, and_12_out, not_9_out);
  and and_13 (and_13_out, and_12_out, not_9_out);
  xor xor_3 (xor_3_out, and_13_out, not_6_out);
  and and_14 (and_14_out, and_13_out, not_6_out);
  xor xor_4 (xor_4_out, and_14_out, not_7_out);
  and and_15 (and_15_out, and_14_out, not_7_out);
  xor xor_5 (xor_5_out, and_15_out, not_3_out);
  and and_16 (and_16_out, and_15_out, not_3_out);
  xor xor_6 (xor_6_out, and_16_out, not_4_out);
  and and_17 (and_17_out, and_16_out, not_4_out);
  xor xor_7 (xor_7_out, and_17_out, not_5_out);
  and and_18 (and_18_out, and_17_out, not_5_out);
  xor xor_8 (xor_8_out, and_18_out, not_2_out);
  and and_19 (and_19_out, and_18_out, not_2_out);
  xor xor_9 (xor_9_out, xor_1_out, in_1[0]);
  and and_20 (and_20_out, xor_1_out, in_1[0]);
  xor xor_10 (xor_10_out, xor_2_out, in_1[1]);
  and and_21 (and_21_out, xor_2_out, in_1[1]);
  xor xor_11 (xor_11_out, xor_3_out, in_1[2]);
  and and_22 (and_22_out, xor_3_out, in_1[2]);
  xor xor_12 (xor_12_out, xor_4_out, in_1[3]);
  and and_23 (and_23_out, xor_4_out, in_1[3]);
  xor xor_13 (xor_13_out, xor_5_out, in_1[4]);
  and and_24 (and_24_out, xor_5_out, in_1[4]);
  xor xor_14 (xor_14_out, xor_6_out, in_1[5]);
  and and_25 (and_25_out, xor_6_out, in_1[5]);
  xor xor_15 (xor_15_out, xor_7_out, in_1[6]);
  and and_26 (and_26_out, xor_7_out, in_1[6]);
  xor xor_16 (xor_16_out, xor_8_out, in_1[7]);
  and and_27 (and_27_out, xor_8_out, in_1[7]);
  xor xor_17 (xor_17_out[0], 1'b0, xor_9_out);
  and and_28 (and_28_out, 1'b0, xor_9_out);
  xor xor_18 (xor_17_out[1], or_6_out, xor_10_out);
  and and_29 (and_29_out, or_6_out, xor_10_out);
  xor xor_19 (xor_17_out[2], or_7_out, xor_11_out);
  and and_30 (and_30_out, or_7_out, xor_11_out);
  xor xor_20 (xor_17_out[3], or_8_out, xor_12_out);
  and and_31 (and_31_out, or_8_out, xor_12_out);
  xor xor_21 (xor_17_out[4], or_9_out, xor_13_out);
  and and_32 (and_32_out, or_9_out, xor_13_out);
  xor xor_22 (xor_17_out[5], or_10_out, xor_14_out);
  and and_33 (and_33_out, or_10_out, xor_14_out);
  xor xor_23 (xor_17_out[6], or_11_out, xor_15_out);
  and and_34 (and_34_out, or_11_out, xor_15_out);
  xor xor_24 (xor_17_out[7], or_12_out, xor_16_out);
  and and_35 (and_35_out, or_12_out, xor_16_out);
  or or_6 (or_6_out, and_28_out, and_20_out);
  or or_7 (or_7_out, and_29_out, and_21_out);
  or or_8 (or_8_out, and_30_out, and_22_out);
  or or_9 (or_9_out, and_31_out, and_23_out);
  or or_10 (or_10_out, and_32_out, and_24_out);
  or or_11 (or_11_out, and_33_out, and_25_out);
  or or_12 (or_12_out, and_34_out, and_26_out);
  or or_13 (or_13_out, and_35_out, and_27_out);
  or or_14 (or_14_out, xor_17_out[3], xor_17_out[4]);
  and and_36 (and_36_out, xor_17_out[1], xor_17_out[2]);
  or or_15 (or_15_out, xor_17_out[1], xor_17_out[2]);
  and and_37 (and_37_out, or_15_out, xor_17_out[3]);
  or or_16 (or_16_out, xor_17_out[2], xor_17_out[3]);
  and and_38 (and_38_out, or_16_out, xor_17_out[4]);
  and and_39 (and_39_out, xor_17_out[1], xor_17_out[2], xor_17_out[3], xor_17_out[4]);
  and and_40 (and_40_out, or_14_out, xor_17_out[5]);
  or or_17 (or_17_out, xor_17_out[1], xor_17_out[2], xor_17_out[3]);
  and and_41 (and_41_out, xor_17_out[4], xor_17_out[5]);
  and and_42 (and_42_out, xor_17_out[2], xor_17_out[3], xor_17_out[4], xor_17_out[5]);
  or or_18 (or_18_out, and_42_out, xor_17_out[6], xor_17_out[7]);
  or or_19 (or_19_out, and_36_out, xor_17_out[3], xor_17_out[4], xor_17_out[5]);
  or or_20 (or_20_out, xor_17_out[4], xor_17_out[5]);
  and and_43 (and_43_out, or_20_out, xor_17_out[6]);
  or or_21 (or_21_out, xor_17_out[1], xor_17_out[2]);
  and and_44 (and_44_out, or_21_out, and_45_out);
  and and_45 (and_45_out, xor_17_out[3], xor_17_out[4]);
  or or_22 (or_22_out, and_37_out, xor_17_out[4], xor_17_out[5], xor_17_out[6], xor_17_out[7]);
  or or_23 (or_23_out, and_38_out, xor_17_out[5], xor_17_out[6], xor_17_out[7]);
  or or_24 (or_24_out, and_39_out, xor_17_out[5], xor_17_out[6], xor_17_out[7]);
  or or_25 (or_25_out, and_40_out, xor_17_out[6], xor_17_out[7]);
  and and_46 (and_46_out, or_17_out, and_41_out);
  and and_47 (and_47_out, or_19_out, xor_17_out[6]);
  or or_26 (or_26_out, and_43_out, xor_17_out[7]);
  or or_27 (or_27_out, and_44_out, xor_17_out[5]);
  xor xor_25 (xor_25_out[3], or_23_out, or_24_out);
  xor xor_26 (xor_26_out[3], or_22_out, or_23_out);
  or or_28 (or_28_out, and_46_out, xor_17_out[6], xor_17_out[7]);
  or or_29 (or_29_out, and_47_out, xor_17_out[7]);
  and and_48 (and_48_out, or_27_out, xor_17_out[6]);
  assign and_49_out = {4{xor_26_out[3]}} & 4'b0001;  // AND_Gate and_49, 4 bits wide
  assign and_50_out = {4{xor_25_out[3]}} & 4'b0010;  // AND_Gate and_50, 4 bits wide
  assign and_51_out = 8'ha & {8{xor_26_out[3]}};  // AND_Gate and_51, 8 bits wide
  xor xor_27 (xor_27_out[3], or_24_out, or_25_out);
  xor xor_28 (xor_28_out[3], or_25_out, or_28_out);
  or or_30 (or_30_out, and_48_out, xor_17_out[7]);
  assign and_52_out = {4{xor_27_out[3]}} & 4'b0011;  // AND_Gate and_52, 4 bits wide
  assign and_53_out = {4{xor_28_out[3]}} & 4'b0100;  // AND_Gate and_53, 4 bits wide
  assign and_54_out = {4{xor_29_out[3]}} & 4'b0101;  // AND_Gate and_54, 4 bits wide
  assign and_55_out = 8'h14 & {8{xor_25_out[3]}};  // AND_Gate and_55, 8 bits wide
  assign and_56_out = 8'h1e & {8{xor_27_out[3]}};  // AND_Gate and_56, 8 bits wide
  xor xor_29 (xor_29_out[3], or_28_out, or_18_out);
  xor xor_30 (xor_30_out[3], or_18_out, or_29_out);
  assign and_57_out = 8'h28 & {8{xor_28_out[3]}};  // AND_Gate and_57, 8 bits wide
  assign and_58_out = 8'h32 & {8{xor_29_out[3]}};  // AND_Gate and_58, 8 bits wide
  xor xor_31 (xor_31_out[3], or_29_out, or_26_out);
  xor xor_32 (xor_32_out[3], or_26_out, or_30_out);
  assign and_59_out = {4{xor_30_out[3]}} & 4'b0110;  // AND_Gate and_59, 4 bits wide
  assign and_60_out = {4{xor_31_out[3]}} & 4'b0111;  // AND_Gate and_60, 4 bits wide
  assign and_61_out = {4{xor_32_out[3]}} & 4'b1000;  // AND_Gate and_61, 4 bits wide
  assign and_62_out = 8'h3c & {8{xor_30_out[3]}};  // AND_Gate and_62, 8 bits wide
  assign and_63_out = 8'h46 & {8{xor_31_out[3]}};  // AND_Gate and_63, 8 bits wide
  xor xor_33 (xor_33_out[7], or_30_out, 1'b0);
  assign and_64_out = 8'h50 & {8{xor_32_out[3]}};  // AND_Gate and_64, 8 bits wide
  assign and_65_out = 8'h5a & {8{xor_33_out[7]}};  // AND_Gate and_65, 8 bits wide
  assign and_66_out = {4{xor_33_out[7]}} & 4'b1001;  // AND_Gate and_66, 4 bits wide
  assign out_2 = 4'b0000 | and_49_out | and_50_out | and_52_out | and_53_out | and_54_out | and_59_out | and_60_out | and_61_out | and_66_out;  // OR_Gate or_31, 4 bits wide
  assign or_32_out = and_51_out | and_55_out | and_56_out | and_57_out | and_58_out | and_62_out | and_63_out | and_64_out | and_65_out | {8{1'b0}};  // OR_Gate or_32, 8 bits wide
  not not_10 (not_10_out, or_32_out[6]);
  not not_11 (not_11_out, or_32_out[7]);
  not not_12 (not_12_out, or_32_out[4]);
  not not_13 (not_13_out, or_32_out[5]);
  not not_14 (not_14_out, or_32_out[1]);
  not not_15 (not_15_out, or_32_out[2]);
  not not_16 (not_16_out, or_32_out[3]);
  not not_17 (not_17_out, or_32_out[0]);
  xor xor_34 (xor_34_out, 1'b1, not_17_out);
  and and_67 (and_67_out, 1'b1, not_17_out);
  xor xor_35 (xor_35_out, and_67_out, not_14_out);
  and and_68 (and_68_out, and_67_out, not_14_out);
  xor xor_36 (xor_36_out, and_68_out, not_15_out);
  and and_69 (and_69_out, and_68_out, not_15_out);
  xor xor_37 (xor_37_out, and_69_out, not_16_out);
  and and_70 (and_70_out, and_69_out, not_16_out);
  xor xor_38 (xor_38_out, and_70_out, not_12_out);
  and and_71 (and_71_out, and_70_out, not_12_out);
  and and_72 (and_72_out, and_71_out, not_13_out);
  and and_73 (and_73_out, and_72_out, not_10_out);
  and and_74 (and_74_out, and_73_out, not_11_out);
  xor xor_39 (xor_39_out, and_71_out, not_13_out);
  xor xor_40 (xor_40_out, and_72_out, not_10_out);
  xor xor_41 (xor_41_out, and_73_out, not_11_out);
  xor xor_42 (xor_42_out, xor_34_out, xor_17_out[0]);
  and and_75 (and_75_out, xor_34_out, xor_17_out[0]);
  xor xor_43 (xor_43_out, xor_35_out, xor_17_out[1]);
  and and_76 (and_76_out, xor_35_out, xor_17_out[1]);
  xor xor_44 (xor_44_out, xor_36_out, xor_17_out[2]);
  and and_77 (and_77_out, xor_36_out, xor_17_out[2]);
  xor xor_45 (xor_45_out, xor_37_out, xor_17_out[3]);
  and and_78 (and_78_out, xor_37_out, xor_17_out[3]);
  xor xor_46 (xor_46_out, xor_38_out, xor_17_out[4]);
  and and_79 (and_79_out, xor_38_out, xor_17_out[4]);
  xor xor_47 (xor_47_out, xor_39_out, xor_17_out[5]);
  and and_80 (and_80_out, xor_39_out, xor_17_out[5]);
  xor xor_48 (xor_48_out, xor_40_out, xor_17_out[6]);
  and and_81 (and_81_out, xor_40_out, xor_17_out[6]);
  xor xor_49 (xor_49_out, xor_41_out, xor_17_out[7]);
  and and_82 (and_82_out, xor_41_out, xor_17_out[7]);
  xor xor_50 (out_3[0], 1'b0, xor_42_out);
  and and_83 (and_83_out, 1'b0, xor_42_out);
  xor xor_51 (out_3[1], or_33_out, xor_43_out);
  and and_84 (and_84_out, or_33_out, xor_43_out);
  xor xor_52 (out_3[2], or_34_out, xor_44_out);
  and and_85 (and_85_out, or_34_out, xor_44_out);
  xor xor_53 (out_3[3], or_35_out, xor_45_out);
  and and_86 (and_86_out, or_35_out, xor_45_out);
  xor xor_54 (xor_54_out[0], or_36_out, xor_46_out);
  and and_87 (and_87_out, or_36_out, xor_46_out);
  xor xor_55 (xor_54_out[1], or_37_out, xor_47_out);
  and and_88 (and_88_out, or_37_out, xor_47_out);
  xor xor_56 (xor_54_out[2], or_38_out, xor_48_out);
  and and_89 (and_89_out, or_38_out, xor_48_out);
  xor xor_57 (xor_54_out[3], or_39_out, xor_49_out);
  and and_90 (and_90_out, or_39_out, xor_49_out);
  or or_33 (or_33_out, and_83_out, and_75_out);
  or or_34 (or_34_out, and_84_out, and_76_out);
  or or_35 (or_35_out, and_85_out, and_77_out);
  or or_36 (or_36_out, and_86_out, and_78_out);
  or or_37 (or_37_out, and_87_out, and_79_out);
  or or_38 (or_38_out, and_88_out, and_80_out);
  or or_39 (or_39_out, and_89_out, and_81_out);
  or or_40 (or_40_out, and_90_out, and_82_out);
endmodule
