// Logisim project BIN2DEC_TEST.circ as structural Verilog: 1 circuit, main circuit main
module main (
  input  [7:0] in_1
);

  wire and_1_out, and_2_out, and_3_out, and_4_out, and_5_out, and_6_out, and_7_out, and_8_out, and_9_out,
       and_10_out, and_11_out, and_12_out, and_13_out, or_1_out, or_2_out, or_3_out, or_4_out, or_5_out,
       or_6_out, or_7_out, or_8_out, or_9_out, or_10_out, or_11_out, or_12_out, or_13_out, or_14_out,
       or_15_out, or_16_out, or_17_out;

  or or_1 (or_1_out, in_1[1], in_1[2]);
  or or_2 (or_2_out, in_1[2], in_1[3]);
  or or_3 (or_3_out, in_1[3], in_1[4]);
  and and_1 (and_1_out, or_3_out, in_1[5]);
  and and_2 (and_2_out, in_1[4], in_1[5]);
  and and_3 (and_3_out, in_1[2], in_1[3], in_1[4], in_1[5]);
  and and_4 (and_4_out, in_1[1], in_1[2]);
  or or_4 (or_4_out, in_1[4], in_1[5]);
  or or_5 (or_5_out, in_1[1], in_1[2]);
  and and_5 (and_5_out, in_1[3], in_1[4]);
  and and_6 (and_6_out, or_1_out, in_1[3]);
  and and_7 (and_7_out, or_2_out, in_1[4]);
  and and_8 (and_8_out, in_1[1], in_1[2], in_1[3], in_1[4]);
  or or_6 (or_6_out, and_1_out, in_1[6], in_1[7]);
  or or_7 (or_7_out, in_1[1], in_1[2], in_1[3]);
  or or_8 (or_8_out, and_3_out, in_1[6], in_1[7]);
  or or_9 (or_9_out, and_4_out, in_1[3], in_1[4], in_1[5]);
  and and_9 (and_9_out, or_4_out, in_1[6]);
  and and_10 (and_10_out, or_5_out, and_5_out);
  or or_10 (or_10_out, and_6_out, in_1[4], in_1[5], in_1[6], in_1[7]);
  or or_11 (or_11_out, and_7_out, in_1[5], in_1[6], in_1[7]);
  or or_12 (or_12_out, and_8_out, in_1[5], in_1[6], in_1[7]);
  and and_11 (and_11_out, or_7_out, and_2_out);
  and and_12 (and_12_out, or_9_out, in_1[6]);
  or or_13 (or_13_out, and_12_out, in_1[7]);
  or or_14 (or_14_out, and_9_out, in_1[7]);
  or or_15 (or_15_out, and_10_out, in_1[5]);
  or or_16 (or_16_out, and_11_out, in_1[6], in_1[7]);
  and and_13 (and_13_out, or_15_out, in_1[6]);
  or or_17 (or_17_out, and_13_out, in_1[7]);
endmodule
