// Logisim project DISTRBT.circ as structural Verilog: 1 circuit, main circuit main
module main (
  input  in_1,
  input  in_2,
  input  in_3,
  input  [7:0] in_4,
  input  [7:0] in_5,
  input  [7:0] in_6,
  input  [7:0] in_7,
  output [7:0] out_8,
  output [7:0] out_9,
  output [7:0] out_10,
  output [7:0] out_11,
  output [7:0] out_12
);

  wire or_1_out, or_3_out, or_5_out, or_7_out, or_9_out, or_11_out, or_13_out, or_15_out, or_17_out,
       or_19_out, or_21_out, or_23_out, or_25_out, or_27_out, or_29_out, or_31_out;
  wire [7:0] and_43_out, and_44_out, and_45_out, and_46_out, and_47_out, and_48_out;

  and and_1 (and_43_out[7], in_4[0], in_3);
  and and_2 (and_44_out[7], in_4[0], in_2);
  and and_3 (and_45_out[7], in_6[0], in_1);
  and and_4 (and_46_out[7], in_6[0], in_3);
  and and_5 (and_47_out[7], in_7[0], in_2);
  and and_6 (and_48_out[7], in_7[0], in_1);
  and and_7 (and_43_out[6], in_4[1], in_3);
  and and_8 (and_44_out[6], in_4[1], in_2);
  and and_9 (and_45_out[6], in_6[1], in_1);
  and and_10 (and_46_out[6], in_6[1], in_3);
  and and_11 (and_47_out[6], in_7[1], in_2);
  and and_12 (and_48_out[6], in_7[1], in_1);
  and and_13 (and_43_out[5], in_4[2], in_3);
  and and_14 (and_44_out[5], in_4[2], in_2);
  and and_15 (and_45_out[5], in_6[2], in_1);
  and and_16 (and_46_out[5], in_6[2], in_3);
  and and_17 (and_47_out[5], in_7[2], in_2);
  and and_18 (and_48_out[5], in_7[2], in_1);
  and and_19 (and_43_out[4], in_4[3], in_3);
  and and_20 (and_44_out[4], in_4[3], in_2);
  and and_21 (and_45_out[4], in_6[3], in_1);
  and and_22 (and_46_out[4], in_6[3], in_3);
  and and_23 (and_47_out[4], in_7[3], in_2);
  and and_24 (and_48_out[4], in_7[3], in_1);
  and and_25 (and_43_out[3], in_4[4], in_3);
  and and_26 (and_44_out[3], in_4[4], in_2);
  and and_27 (and_45_out[3], in_6[4], in_1);
  and and_28 (and_46_out[3], in_6[4], in_3);
  and and_29 (and_47_out[3], in_7[4], in_2);
  and and_30 (and_48_out[3], in_7[4], in_1);
  and and_31 (and_43_out[2], in_4[5], in_3);
  and and_32 (and_44_out[2], in_4[5], in_2);
  and and_33 (and_45_out[2], in_6[5], in_1);
  and and_34 (and_46_out[2], in_6[5], in_3);
  and and_35 (and_47_out[2], in_7[5], in_2);
  and and_36 (and_48_out[2], in_7[5], in_1);
  and and_37 (and_43_out[1], in_4[6], in_3);
  and and_38 (and_44_out[1], in_4[6], in_2);
  and and_39 (and_45_out[1], in_6[6], in_1);
  and and_40 (and_46_out[1], in_6[6], in_3);
  and and_41 (and_47_out[1], in_7[6], in_2);
  and and_42 (and_48_out[1], in_7[6], in_1);
  and and_43 (and_43_out[0], in_4[7], in_3);
  and and_44 (and_44_out[0], in_4[7], in_2);
  and and_45 (and_45_out[0], in_6[7], in_1);
  and and_46 (and_46_out[0], in_6[7], in_3);
  and and_47 (and_47_out[0], in_7[7], in_2);
  and and_48 (and_48_out[0], in_7[7], in_1);
  or or_1 (or_1_out, and_47_out[7], and_45_out[7]);
  or or_2 (out_8[7], or_1_out, and_43_out[7]);
  or or_3 (or_3_out, and_48_out[7], and_46_out[7]);
  or or_4 (out_11[7], or_3_out, and_44_out[7]);
  or or_5 (or_5_out, and_47_out[6], and_45_out[6]);
  or or_6 (out_8[6], or_5_out, and_43_out[6]);
  or or_7 (or_7_out, and_48_out[6], and_46_out[6]);
  or or_8 (out_11[6], or_7_out, and_44_out[6]);
  or or_9 (or_9_out, and_47_out[5], and_45_out[5]);
  or or_10 (out_8[5], or_9_out, and_43_out[5]);
  or or_11 (or_11_out, and_48_out[5], and_46_out[5]);
  or or_12 (out_11[5], or_11_out, and_44_out[5]);
  or or_13 (or_13_out, and_47_out[4], and_45_out[4]);
  or or_14 (out_8[4], or_13_out, and_43_out[4]);
  or or_15 (or_15_out, and_48_out[4], and_46_out[4]);
  or or_16 (out_11[4], or_15_out, and_44_out[4]);
  or or_17 (or_17_out, and_47_out[3], and_45_out[3]);
  or or_18 (out_8[3], or_17_out, and_43_out[3]);
  or or_19 (or_19_out, and_48_out[3], and_46_out[3]);
  or or_20 (out_11[3], or_19_out, and_44_out[3]);
  or or_21 (or_21_out, and_47_out[2], and_45_out[2]);
  or or_22 (out_8[2], or_21_out, and_43_out[2]);
  or or_23 (or_23_out, and_48_out[2], and_46_out[2]);
  or or_24 (out_11[2], or_23_out, and_44_out[2]);
  or or_25 (or_25_out, and_47_out[1], and_45_out[1]);
  or or_26 (out_8[1], or_25_out, and_43_out[1]);
  or or_27 (or_27_out, and_48_out[1], and_46_out[1]);
  or or_28 (out_11[1], or_27_out, and_44_out[1]);
  or or_29 (or_29_out, and_47_out[0], and_45_out[0]);
  or or_30 (out_8[0], or_29_out, and_43_out[0]);
  or or_31 (or_31_out, and_48_out[0], and_46_out[0]);
  or or_32 (out_11[0], or_31_out, and_44_out[0]);
  and and_49 (out_9[7], in_5[0], in_1);
  and and_50 (out_10[7], in_5[0], in_2);
  and and_51 (out_12[7], in_5[0], in_3);
  and and_52 (out_9[6], in_5[1], in_1);
  and and_53 (out_10[6], in_5[1], in_2);
  and and_54 (out_12[6], in_5[1], in_3);
  and and_55 (out_9[5], in_5[2], in_1);
  and and_56 (out_10[5], in_5[2], in_2);
  and and_57 (out_12[5], in_5[2], in_3);
  and and_58 (out_9[4], in_5[3], in_1);
  and and_59 (out_10[4], in_5[3], in_2);
  and and_60 (out_12[4], in_5[3], in_3);
  and and_61 (out_9[3], in_5[4], in_1);
  and and_62 (out_10[3], in_5[4], in_2);
  and and_63 (out_12[3], in_5[4], in_3);
  and and_64 (out_9[2], in_5[5], in_1);
  and and_65 (out_10[2], in_5[5], in_2);
  and and_66 (out_12[2], in_5[5], in_3);
  and and_67 (out_9[1], in_5[6], in_1);
  and and_68 (out_10[1], in_5[6], in_2);
  and and_69 (out_12[1], in_5[6], in_3);
  and and_70 (out_9[0], in_5[7], in_1);
  and and_71 (out_10[0], in_5[7], in_2);
  and and_72 (out_12[0], in_5[7], in_3);
endmodule
