// Logisim project EXAMPLE OF DISTRIBUTOR.circ as structural Verilog: 1 circuit, main circuit main
module main (
  input  [7:0] in_1,
  input  [7:0] in_2,
  input  [7:0] in_3,
  input  in_4,
  input  in_5,
  input  in_6,
  output [7:0] out_7,
  output [7:0] out_8,
  output [7:0] out_9
);

  wire [7:0] main_1_out_8, main_1_out_11, or_1_out;

  DISTRBT_main main_1 (
    .in_1(in_4), .in_2(in_5), .in_3(in_6), .in_4(in_1), .in_5(or_1_out), .in_6(in_2), .in_7(in_3),
    .out_8(main_1_out_8), .out_9(out_7), .out_10(out_8), .out_11(main_1_out_11), .out_12(out_9));
  assign or_1_out = main_1_out_11 | main_1_out_8;  // OR_Gate or_1, 8 bits wide
endmodule
