// Logisim project INP SEL.circ as structural Verilog: 1 circuit, main circuit main
module main (
  input  [7:0] in_1,
  input  [7:0] in_2,
  input  [7:0] in_3,
  input  in_4,
  input  [7:0] in_5,
  input  [7:0] in_6,
  input  [7:0] in_7,
  output [7:0] out_8,
  output [7:0] out_9,
  output [7:0] out_10
);

  wire [7:0] and_1_out, and_2_out, and_3_out, and_4_out, and_5_out, and_6_out;
  wire [7:7] not_1_out;

  not not_1 (not_1_out[7], in_4);
  assign and_1_out = in_1 & {8{not_1_out[7]}};  // AND_Gate and_1, 8 bits wide
  assign and_2_out = {8{in_4}} & in_5;  // AND_Gate and_2, 8 bits wide
  assign and_3_out = in_2 & {8{not_1_out[7]}};  // AND_Gate and_3, 8 bits wide
  assign out_8 = and_1_out | and_2_out;  // OR_Gate or_1, 8 bits wide
  assign and_4_out = {8{in_4}} & in_6;  // AND_Gate and_4, 8 bits wide
  assign and_5_out = in_3 & {8{not_1_out[7]}};  // AND_Gate and_5, 8 bits wide
  assign out_9 = and_3_out | and_4_out;  // OR_Gate or_2, 8 bits wide
  assign and_6_out = {8{in_4}} & in_7;  // AND_Gate and_6, 8 bits wide
  assign out_10 = and_5_out | and_6_out;  // OR_Gate or_3, 8 bits wide
endmodule
