// Logisim project INSTRCTR.circ as structural Verilog: 1 circuit, main circuit main
module main (
  input  [3:0] in_1,
  output [14:0] out_2
);

  wire and_1_out, and_2_out, and_3_out, and_4_out, and_5_out, and_6_out, and_7_out, and_8_out, and_9_out,
       and_10_out, and_11_out, and_12_out, and_13_out, and_14_out, and_15_out, and_16_out, and_18_out,
       and_20_out, and_22_out, and_24_out, and_26_out, and_28_out, and_30_out, and_32_out, and_34_out,
       and_36_out, and_38_out, and_40_out, and_42_out, and_44_out;
  wire [3:0] xnor_1_out, xnor_2_out, xnor_3_out, xnor_4_out, xnor_5_out, xnor_6_out, xnor_7_out, xnor_8_out,
       xnor_9_out, xnor_10_out, xnor_11_out, xnor_12_out, xnor_13_out, xnor_14_out, xnor_15_out;

  assign xnor_1_out = ~(in_1 ^ 4'b0001);  // XNOR_Gate xnor_1, 4 bits wide
  assign xnor_2_out = ~(in_1 ^ 4'b0010);  // XNOR_Gate xnor_2, 4 bits wide
  assign xnor_3_out = ~(in_1 ^ 4'b0011);  // XNOR_Gate xnor_3, 4 bits wide
  assign xnor_4_out = ~(in_1 ^ 4'b0100);  // XNOR_Gate xnor_4, 4 bits wide
  assign xnor_5_out = ~(in_1 ^ 4'b0101);  // XNOR_Gate xnor_5, 4 bits wide
  assign xnor_6_out = ~(in_1 ^ 4'b0110);  // XNOR_Gate xnor_6, 4 bits wide
  assign xnor_7_out = ~(in_1 ^ 4'b0111);  // XNOR_Gate xnor_7, 4 bits wide
  assign xnor_8_out = ~(in_1 ^ 4'b1000);  // XNOR_Gate xnor_8, 4 bits wide
  assign xnor_9_out = ~(in_1 ^ 4'b1001);  // XNOR_Gate xnor_9, 4 bits wide
  assign xnor_10_out = ~(in_1 ^ 4'b1010);  // XNOR_Gate xnor_10, 4 bits wide
  assign xnor_11_out = ~(in_1 ^ 4'b1011);  // XNOR_Gate xnor_11, 4 bits wide
  assign xnor_12_out = ~(in_1 ^ 4'b1100);  // XNOR_Gate xnor_12, 4 bits wide
  assign xnor_13_out = ~(in_1 ^ 4'b1101);  // XNOR_Gate xnor_13, 4 bits wide
  assign xnor_14_out = ~(in_1 ^ 4'b1110);  // XNOR_Gate xnor_14, 4 bits wide
  assign xnor_15_out = ~(in_1 ^ 4'b1111);  // XNOR_Gate xnor_15, 4 bits wide
  and and_1 (and_1_out, xnor_1_out[2], xnor_1_out[3]);
  and and_2 (and_2_out, xnor_2_out[2], xnor_2_out[3]);
  and and_3 (and_3_out, xnor_3_out[2], xnor_3_out[3]);
  and and_4 (and_4_out, xnor_4_out[2], xnor_4_out[3]);
  and and_5 (and_5_out, xnor_5_out[2], xnor_5_out[3]);
  and and_6 (and_6_out, xnor_6_out[2], xnor_6_out[3]);
  and and_7 (and_7_out, xnor_7_out[2], xnor_7_out[3]);
  and and_8 (and_8_out, xnor_8_out[2], xnor_8_out[3]);
  and and_9 (and_9_out, xnor_9_out[2], xnor_9_out[3]);
  and and_10 (and_10_out, xnor_10_out[2], xnor_10_out[3]);
  and and_11 (and_11_out, xnor_11_out[2], xnor_11_out[3]);
  and and_12 (and_12_out, xnor_12_out[2], xnor_12_out[3]);
  and and_13 (and_13_out, xnor_13_out[2], xnor_13_out[3]);
  and and_14 (and_14_out, xnor_14_out[2], xnor_14_out[3]);
  and and_15 (and_15_out, xnor_15_out[2], xnor_15_out[3]);
  and and_16 (and_16_out, xnor_1_out[1], and_1_out);
  and and_17 (out_2[0], xnor_1_out[0], and_16_out);
  and and_18 (and_18_out, xnor_2_out[1], and_2_out);
  and and_19 (out_2[1], xnor_2_out[0], and_18_out);
  and and_20 (and_20_out, xnor_3_out[1], and_3_out);
  and and_21 (out_2[2], xnor_3_out[0], and_20_out);
  and and_22 (and_22_out, xnor_4_out[1], and_4_out);
  and and_23 (out_2[3], xnor_4_out[0], and_22_out);
  and and_24 (and_24_out, xnor_5_out[1], and_5_out);
  and and_25 (out_2[4], xnor_5_out[0], and_24_out);
  and and_26 (and_26_out, xnor_6_out[1], and_6_out);
  and and_27 (out_2[5], xnor_6_out[0], and_26_out);
  and and_28 (and_28_out, xnor_7_out[1], and_7_out);
  and and_29 (out_2[6], xnor_7_out[0], and_28_out);
  and and_30 (and_30_out, xnor_8_out[1], and_8_out);
  and and_31 (out_2[7], xnor_8_out[0], and_30_out);
  and and_32 (and_32_out, xnor_9_out[1], and_9_out);
  and and_33 (out_2[8], xnor_9_out[0], and_32_out);
  and and_34 (and_34_out, xnor_10_out[1], and_10_out);
  and and_35 (out_2[9], xnor_10_out[0], and_34_out);
  and and_36 (and_36_out, xnor_11_out[1], and_11_out);
  and and_37 (out_2[10], xnor_11_out[0], and_36_out);
  and and_38 (and_38_out, xnor_12_out[1], and_12_out);
  and and_39 (out_2[11], xnor_12_out[0], and_38_out);
  and and_40 (and_40_out, xnor_13_out[1], and_13_out);
  and and_41 (out_2[12], xnor_13_out[0], and_40_out);
  and and_42 (and_42_out, xnor_14_out[1], and_14_out);
  and and_43 (out_2[13], xnor_14_out[0], and_42_out);
  and and_44 (and_44_out, xnor_15_out[1], and_15_out);
  and and_45 (out_2[14], xnor_15_out[0], and_44_out);
endmodule
