// Logisim project RAM.circ as structural Verilog: 1 circuit, main circuit main
module main (
  input  [9:0] in_1,
  input  in_2,
  input  [7:0] in_3,
  input  in_4,
  output [7:0] out_5
);

  wire and_5_out, and_6_out, and_7_out, not_1_out, not_2_out, not_3_out, not_4_out;
  wire [3:0] and_10_out, and_11_out, and_16_out, and_19_out;
  wire [7:0] controlled_buffer_1_out, ram_1_data;

  or or_1 (out_5[3], and_16_out[3], and_11_out[3]);
  or or_2 (out_5[7], and_19_out[3], and_10_out[3]);
  or or_3 (out_5[1], and_16_out[1], and_11_out[1]);
  or or_4 (out_5[2], and_16_out[2], and_11_out[2]);
  or or_5 (out_5[6], and_19_out[2], and_10_out[2]);
  or or_6 (out_5[5], and_19_out[1], and_10_out[1]);
  or or_7 (out_5[0], and_16_out[0], and_11_out[0]);
  or or_8 (out_5[4], and_19_out[0], and_10_out[0]);
  and and_1 (and_10_out[3], and_5_out, in_1[7]);
  and and_2 (and_11_out[3], and_5_out, in_1[3]);
  not not_1 (not_1_out, in_1[9]);
  not not_2 (not_2_out, in_1[8]);
  and and_3 (and_10_out[2], and_5_out, in_1[6]);
  and and_4 (and_11_out[2], and_5_out, in_1[2]);
  not not_3 (not_3_out, and_7_out);
  not not_4 (not_4_out, in_2);
  and and_5 (and_5_out, in_1[8], in_1[9]);
  and and_6 (and_6_out, in_1[8], not_1_out);
  and and_7 (and_7_out, not_2_out, in_1[9]);
  and and_8 (and_10_out[1], and_5_out, in_1[5]);
  and and_9 (and_11_out[1], and_5_out, in_1[1]);
  assign controlled_buffer_1_out = and_6_out ? ram_1_data : 8'bz;  // Controlled_Buffer controlled_buffer_1
  RAM #(.addrWidth(4)) ram_1 (
    .addr(in_1[3:0]), .data(ram_1_data), .sel(1'b1), .clk(not_4_out), .ld(not_3_out), .clr(in_4));
  assign ram_1_data = and_7_out ? in_3 : 8'bz;  // Controlled_Buffer controlled_buffer_2
  and and_10 (and_10_out[0], and_5_out, in_1[4]);
  and and_11 (and_11_out[0], and_5_out, in_1[0]);
  and and_12 (and_16_out[3], and_6_out, controlled_buffer_1_out[3]);
  and and_13 (and_19_out[3], and_6_out, controlled_buffer_1_out[7]);
  and and_14 (and_16_out[2], and_6_out, controlled_buffer_1_out[2]);
  and and_15 (and_19_out[2], and_6_out, controlled_buffer_1_out[6]);
  and and_16 (and_16_out[0], and_6_out, controlled_buffer_1_out[0]);
  and and_17 (and_16_out[1], and_6_out, controlled_buffer_1_out[1]);
  and and_18 (and_19_out[1], and_6_out, controlled_buffer_1_out[5]);
  and and_19 (and_19_out[0], and_6_out, controlled_buffer_1_out[4]);
endmodule
