// Logisim project SFTRGT.circ as structural Verilog: 1 circuit, main circuit main
module main (
  input  [7:0] in_1,
  input  [7:0] in_2,
  output [7:0] out_3
);

  wire or_8_out;

  or or_1 (out_3[6], in_1[7], in_2[7]);
  or or_2 (out_3[5], in_1[6], in_2[6]);
  or or_3 (out_3[4], in_1[5], in_2[5]);
  or or_4 (out_3[3], in_1[4], in_2[4]);
  or or_5 (out_3[2], in_1[3], in_2[3]);
  or or_6 (out_3[1], in_1[2], in_2[2]);
  or or_7 (out_3[0], in_1[1], in_2[1]);
  or or_8 (or_8_out, in_1[0], in_2[0]);

  assign out_3[7] = 1'b0;
endmodule
