// Logisim project STEP SELEC.circ as structural Verilog: 1 circuit, main circuit main
module main (
  input  [7:0] in_1,
  input  [7:0] in_2,
  input  [7:0] in_3,
  output [7:0] out_4
);

  wire and_1_out, and_2_out, and_3_out, and_4_out, and_5_out, and_6_out, and_7_out, and_8_out, and_9_out,
       and_10_out, and_11_out, and_12_out, and_13_out, and_14_out, and_15_out, and_16_out, and_17_out,
       and_18_out, and_19_out, and_20_out, and_21_out, and_22_out, and_23_out, not_1_out;

  and and_1 (and_1_out, in_2[6], in_2[7]);
  and and_2 (and_2_out, and_1_out, in_2[5]);
  and and_3 (and_3_out, and_2_out, in_2[4]);
  and and_4 (and_4_out, and_3_out, in_2[3]);
  and and_5 (and_5_out, and_4_out, in_2[2]);
  and and_6 (and_6_out, and_5_out, in_2[1]);
  and and_7 (and_7_out, and_6_out, in_2[0]);
  not not_1 (not_1_out, and_7_out);
  and and_8 (and_8_out, in_1[7], not_1_out);
  and and_9 (and_9_out, and_7_out, in_3[7]);
  and and_10 (and_10_out, in_1[6], not_1_out);
  or or_1 (out_4[7], and_8_out, and_9_out);
  and and_11 (and_11_out, and_7_out, in_3[6]);
  and and_12 (and_12_out, in_1[5], not_1_out);
  or or_2 (out_4[6], and_10_out, and_11_out);
  and and_13 (and_13_out, and_7_out, in_3[5]);
  and and_14 (and_14_out, in_1[4], not_1_out);
  or or_3 (out_4[5], and_12_out, and_13_out);
  and and_15 (and_15_out, and_7_out, in_3[4]);
  or or_4 (out_4[4], and_14_out, and_15_out);
  and and_16 (and_16_out, in_1[3], not_1_out);
  and and_17 (and_17_out, and_7_out, in_3[3]);
  and and_18 (and_18_out, in_1[2], not_1_out);
  or or_5 (out_4[3], and_16_out, and_17_out);
  and and_19 (and_19_out, and_7_out, in_3[2]);
  and and_20 (and_20_out, in_1[1], not_1_out);
  or or_6 (out_4[2], and_18_out, and_19_out);
  and and_21 (and_21_out, and_7_out, in_3[1]);
  or or_7 (out_4[1], and_20_out, and_21_out);
  and and_22 (and_22_out, in_1[0], not_1_out);
  and and_23 (and_23_out, and_7_out, in_3[0]);
  or or_8 (out_4[0], and_22_out, and_23_out);
endmodule
