// Logisim project Stopwatch Demo.circ as structural Verilog: 1 circuit, main circuit main
module main (
  input  Stop_Start
);

  wire and_1_out, clock_1_out;
  wire [3:0] main_1_out_2, main_1_out_3, main_1_out_4;
  wire [7:0] counter_1_q;

  Clock clock_1 (.out(clock_1_out));
  and and_1 (and_1_out, Stop_Start, clock_1_out);
  Counter counter_1 (.Q(counter_1_q), .clk(and_1_out));  // open: load, D, count, carry, clr
  Hex_Digit_Display hex_digit_display_1 (.value(main_1_out_2));  // open: dp
  Hex_Digit_Display hex_digit_display_2 (.value(main_1_out_4));  // open: dp
  BIN2DEC_main main_1 (.out_3(main_1_out_3), .in_1(counter_1_q), .out_2(main_1_out_2), .out_4(main_1_out_4));
  Hex_Digit_Display hex_digit_display_3 (.value(main_1_out_3));  // open: dp
endmodule
