// Logisim project XNOR.circ as structural Verilog: 1 circuit, main circuit main
module main (
  input  [7:0] in_1,
  input  [7:0] in_2,
  output [7:0] out_3
);

  xnor xnor_1 (out_3[7], in_1[7], in_2[7]);
  xnor xnor_2 (out_3[6], in_1[6], in_2[6]);
  xnor xnor_3 (out_3[5], in_1[5], in_2[5]);
  xnor xnor_4 (out_3[4], in_1[4], in_2[4]);
  xnor xnor_5 (out_3[3], in_1[3], in_2[3]);
  xnor xnor_6 (out_3[2], in_1[2], in_2[2]);
  xnor xnor_7 (out_3[1], in_1[1], in_2[1]);
  xnor xnor_8 (out_3[0], in_1[0], in_2[0]);
endmodule
