// Logisim project XOR.circ as structural Verilog: 1 circuit, main circuit main
module main (
  input  [7:0] in_1,
  input  [7:0] in_2,
  output [7:0] out_3
);

  xor xor_1 (out_3[7], in_1[7], in_2[7]);
  xor xor_2 (out_3[6], in_1[6], in_2[6]);
  xor xor_3 (out_3[5], in_1[5], in_2[5]);
  xor xor_4 (out_3[4], in_1[4], in_2[4]);
  xor xor_5 (out_3[3], in_1[3], in_2[3]);
  xor xor_6 (out_3[2], in_1[2], in_2[2]);
  xor xor_7 (out_3[1], in_1[1], in_2[1]);
  xor xor_8 (out_3[0], in_1[0], in_2[0]);
endmodule
