// Logisim project rcd.circ as structural Verilog: 1 circuit, main circuit main
module main (
  input  [7:0] in_1,
  input  [7:0] in_2,
  input  [7:0] in_3,
  output [7:0] out_4,
  output [7:0] out_5,
  output [7:0] out_6
);

  wire button_1_out, clock_1_out, controlled_buffer_1_out, not_1_out, not_2_out;
  wire [3:0] main_2_out_5, main_2_out_5_2, main_13_out_5, main_13_out_5_2, main_14_out_5, main_14_out_5_2,
       rom_1_data;
  wire [4:4] rom_1_data_2;
  wire [7:0] counter_1_q, main_3_out_4, main_4_to_a, main_4_to_b, main_4_to_c, main_5_out_3, main_6_out_3,
       main_7_out_3, main_8_out_3, main_9_out_3, main_10_out_3, main_11_out_3, main_12_out_3, main_15_out_8,
       main_15_out_9, main_15_out_10, main_16_out_8, main_16_out_9, main_16_out_10, main_17_out_8,
       main_17_out_9, main_17_out_10, main_18_out_8, main_18_out_9, main_18_out_10, main_19_out_8,
       main_19_out_9, main_19_out_10, main_20_out_8, main_20_out_9, main_20_out_10, main_21_out_8,
       main_21_out_9, main_21_out_10, main_22_out_8, main_22_out_9, main_22_out_10, main_23_out_8,
       main_23_out_9, main_23_out_10, main_24_out_8, main_24_out_9, main_24_out_10;
  wire [9:0] rom_2_data;
  wire [14:0] main_1_out_2;
  wire [29:10] rom_2_data_2;

  Button button_1 (.out(button_1_out));
  Clock clock_1 (.out(clock_1_out));
  not not_1 (not_1_out, main_1_out_2[9]);
  not not_2 (not_2_out, rom_1_data_2[4]);
  assign controlled_buffer_1_out = not_2_out ? clock_1_out : 1'bz;  // Controlled_Buffer controlled_buffer_1
  Hex_Digit_Display hex_digit_display_1 (.value(main_2_out_5_2));  // open: dp
  Hex_Digit_Display hex_digit_display_2 (.value(main_2_out_5));  // open: dp
  Counter counter_1 (
    .load(main_1_out_2[9]), .D(main_3_out_4), .count(not_1_out), .Q(counter_1_q),
    .clk(controlled_buffer_1_out), .clr(button_1_out));  // open: carry
  Hex_Digit_Display hex_digit_display_3 (.value(main_13_out_5_2));  // open: dp
  Hex_Digit_Display hex_digit_display_4 (.value(main_13_out_5));  // open: dp
  Hex_Digit_Display hex_digit_display_5 (.value(main_14_out_5_2));  // open: dp
  Hex_Digit_Display hex_digit_display_6 (.value(main_14_out_5));  // open: dp
  ROM #(.dataWidth(5)) rom_1 (.addr(counter_1_q), .data({rom_1_data_2[4], rom_1_data}));  // open: sel
  assign {out_6, out_5, out_4} = main_1_out_2[11] ? {main_2_out_5_2, main_2_out_5, main_13_out_5_2, main_13_out_5, main_14_out_5_2, main_14_out_5} : 24'bz;  // Controlled_Buffer controlled_buffer_2
  INSTRCTR_main main_1 (.in_1(rom_1_data), .out_2(main_1_out_2));
  ROM #(.dataWidth(30)) rom_2 (.addr(counter_1_q), .data({rom_2_data_2, rom_2_data}));  // open: sel
  RAM_main main_2 (
    .out_5({main_2_out_5_2, main_2_out_5}), .in_1(rom_2_data_2[29:20]), .in_2(controlled_buffer_1_out),
    .in_3(main_24_out_8), .in_4(button_1_out));
  DotMatrix #(.matrixcols(24), .matrixrows(1)) dotmatrix_1 (
    .col0(main_24_out_8[7]), .col1(main_24_out_8[6]), .col2(main_24_out_8[5]), .col3(main_24_out_8[4]),
    .col4(main_24_out_8[3]), .col5(main_24_out_8[2]), .col6(main_24_out_8[1]), .col7(main_24_out_8[0]),
    .col8(main_24_out_9[7]), .col9(main_24_out_9[6]), .col10(main_24_out_9[5]), .col11(main_24_out_9[4]),
    .col12(main_24_out_9[3]), .col13(main_24_out_9[2]), .col14(main_24_out_9[1]), .col15(main_24_out_9[0]),
    .col16(main_24_out_10[7]), .col17(main_24_out_10[6]), .col18(main_24_out_10[5]),
    .col19(main_24_out_10[4]), .col20(main_24_out_10[3]), .col21(main_24_out_10[2]),
    .col22(main_24_out_10[1]), .col23(main_24_out_10[0]));
  STEP_SELEC_main main_3 (
    .in_2({main_2_out_5_2, main_2_out_5}), .in_3({main_13_out_5_2, main_13_out_5}), .out_4(main_3_out_4),
    .in_1({main_14_out_5_2, main_14_out_5}));
  VAL_TRNSFR_main main_4 (
    .Inp_A({main_2_out_5_2, main_2_out_5}), .Inp_C({main_14_out_5_2, main_14_out_5}),
    .Inp_B({main_13_out_5_2, main_13_out_5}), .To_B(main_4_to_b), .To_A(main_4_to_a), .To_C(main_4_to_c));
  SFTRGT_main main_5 (
    .in_1({main_2_out_5_2, main_2_out_5}), .in_2({main_13_out_5_2, main_13_out_5}), .out_3(main_5_out_3));
  SFTLFT_main main_6 (
    .in_1({main_2_out_5_2, main_2_out_5}), .in_2({main_13_out_5_2, main_13_out_5}), .out_3(main_6_out_3));
  XNOR_main main_7 (
    .in_1({main_2_out_5_2, main_2_out_5}), .in_2({main_13_out_5_2, main_13_out_5}), .out_3(main_7_out_3));
  XOR_main main_8 (
    .in_1({main_2_out_5_2, main_2_out_5}), .in_2({main_13_out_5_2, main_13_out_5}), .out_3(main_8_out_3));
  NOR_main main_9 (
    .in_1({main_2_out_5_2, main_2_out_5}), .in_2({main_13_out_5_2, main_13_out_5}), .out_3(main_9_out_3));
  NAND_main main_10 (
    .in_1({main_2_out_5_2, main_2_out_5}), .in_2({main_13_out_5_2, main_13_out_5}), .out_3(main_10_out_3));
  OR_main main_11 (
    .in_1({main_2_out_5_2, main_2_out_5}), .in_2({main_13_out_5_2, main_13_out_5}), .out_3(main_11_out_3));
  AND_main main_12 (
    .in_1({main_2_out_5_2, main_2_out_5}), .in_2({main_13_out_5_2, main_13_out_5}), .out_3(main_12_out_3));
  DotMatrix #(.matrixcols(30), .matrixrows(1)) dotmatrix_2 (
    .col0(rom_2_data_2[29]), .col1(rom_2_data_2[28]), .col2(rom_2_data_2[27]), .col3(rom_2_data_2[26]),
    .col4(rom_2_data_2[25]), .col5(rom_2_data_2[24]), .col6(rom_2_data_2[23]), .col7(rom_2_data_2[22]),
    .col8(rom_2_data_2[21]), .col9(rom_2_data_2[20]), .col10(rom_2_data_2[19]), .col11(rom_2_data_2[18]),
    .col12(rom_2_data_2[17]), .col13(rom_2_data_2[16]), .col14(rom_2_data_2[15]), .col15(rom_2_data_2[14]),
    .col16(rom_2_data_2[13]), .col17(rom_2_data_2[12]), .col18(rom_2_data_2[11]), .col19(rom_2_data_2[10]),
    .col20(rom_2_data[9]), .col21(rom_2_data[8]), .col22(rom_2_data[7]), .col23(rom_2_data[6]),
    .col24(rom_2_data[5]), .col25(rom_2_data[4]), .col26(rom_2_data[3]), .col27(rom_2_data[2]),
    .col28(rom_2_data[1]), .col29(rom_2_data[0]));
  RAM_main main_13 (
    .out_5({main_13_out_5_2, main_13_out_5}), .in_1(rom_2_data_2[19:10]), .in_2(controlled_buffer_1_out),
    .in_3(main_24_out_9), .in_4(button_1_out));
  DotMatrix #(.matrixcols(24), .matrixrows(1)) dotmatrix_3 (
    .col0(main_2_out_5_2[3]), .col1(main_2_out_5_2[2]), .col2(main_2_out_5_2[1]), .col3(main_2_out_5_2[0]),
    .col4(main_2_out_5[3]), .col5(main_2_out_5[2]), .col6(main_2_out_5[1]), .col7(main_2_out_5[0]),
    .col8(main_13_out_5_2[3]), .col9(main_13_out_5_2[2]), .col10(main_13_out_5_2[1]),
    .col11(main_13_out_5_2[0]), .col12(main_13_out_5[3]), .col13(main_13_out_5[2]), .col14(main_13_out_5[1]),
    .col15(main_13_out_5[0]), .col16(main_14_out_5_2[3]), .col17(main_14_out_5_2[2]),
    .col18(main_14_out_5_2[1]), .col19(main_14_out_5_2[0]), .col20(main_14_out_5[3]),
    .col21(main_14_out_5[2]), .col22(main_14_out_5[1]), .col23(main_14_out_5[0]));
  RAM_main main_14 (
    .out_5({main_14_out_5_2, main_14_out_5}), .in_1(rom_2_data), .in_2(controlled_buffer_1_out),
    .in_3(main_24_out_10), .in_4(button_1_out));
  INP_SEL_main main_15 (
    .in_1({8{1'b0}}), .in_2({8{1'b0}}), .in_3({8{1'b0}}), .in_4(main_1_out_2[10]), .out_8(main_15_out_8),
    .out_9(main_15_out_9), .out_10(main_15_out_10), .in_5(in_1), .in_6(in_2), .in_7(in_3));
  INP_SEL_main main_16 (
    .in_1(main_15_out_8), .in_2(main_15_out_9), .in_3(main_15_out_10), .in_4(main_1_out_2[8]),
    .out_8(main_16_out_8), .out_9(main_16_out_9), .out_10(main_16_out_10), .in_5(main_4_to_a),
    .in_6(main_4_to_b), .in_7(main_4_to_c));
  INP_SEL_main main_17 (
    .in_1(main_16_out_8), .in_2(main_16_out_9), .in_3(main_16_out_10), .in_4(main_1_out_2[7]),
    .out_8(main_17_out_8), .out_9(main_17_out_9), .out_10(main_17_out_10), .in_5({8{1'b0}}),
    .in_6({8{1'b0}}), .in_7(main_5_out_3));
  INP_SEL_main main_18 (
    .in_1(main_17_out_8), .in_2(main_17_out_9), .in_3(main_17_out_10), .in_4(main_1_out_2[6]),
    .out_8(main_18_out_8), .out_9(main_18_out_9), .out_10(main_18_out_10), .in_5({8{1'b0}}),
    .in_6({8{1'b0}}), .in_7(main_6_out_3));
  INP_SEL_main main_19 (
    .in_1(main_18_out_8), .in_2(main_18_out_9), .in_3(main_18_out_10), .in_4(main_1_out_2[5]),
    .out_8(main_19_out_8), .out_9(main_19_out_9), .out_10(main_19_out_10), .in_5({8{1'b0}}),
    .in_6({8{1'b0}}), .in_7(main_7_out_3));
  INP_SEL_main main_20 (
    .in_1(main_19_out_8), .in_2(main_19_out_9), .in_3(main_19_out_10), .in_4(main_1_out_2[4]),
    .out_8(main_20_out_8), .out_9(main_20_out_9), .out_10(main_20_out_10), .in_5({8{1'b0}}),
    .in_6({8{1'b0}}), .in_7(main_8_out_3));
  INP_SEL_main main_21 (
    .in_1(main_20_out_8), .in_2(main_20_out_9), .in_3(main_20_out_10), .in_4(main_1_out_2[3]),
    .out_8(main_21_out_8), .out_9(main_21_out_9), .out_10(main_21_out_10), .in_5({8{1'b0}}),
    .in_6({8{1'b0}}), .in_7(main_9_out_3));
  INP_SEL_main main_22 (
    .in_1(main_21_out_8), .in_2(main_21_out_9), .in_3(main_21_out_10), .in_4(main_1_out_2[2]),
    .out_8(main_22_out_8), .out_9(main_22_out_9), .out_10(main_22_out_10), .in_5({8{1'b0}}),
    .in_6({8{1'b0}}), .in_7(main_10_out_3));
  INP_SEL_main main_23 (
    .in_1(main_22_out_8), .in_2(main_22_out_9), .in_3(main_22_out_10), .in_4(main_1_out_2[1]),
    .out_8(main_23_out_8), .out_9(main_23_out_9), .out_10(main_23_out_10), .in_5({8{1'b0}}),
    .in_6({8{1'b0}}), .in_7(main_11_out_3));
  INP_SEL_main main_24 (
    .in_1(main_23_out_8), .in_2(main_23_out_9), .in_3(main_23_out_10), .in_4(main_1_out_2[0]),
    .out_8(main_24_out_8), .out_9(main_24_out_9), .out_10(main_24_out_10), .in_5({8{1'b0}}),
    .in_6({8{1'b0}}), .in_7(main_12_out_3));

  // Notes on the sheet:
  //   contents of rom_1 (hex, n*v repeats v):
  //   0 1 c
  //   contents of rom_2 (hex, n*v repeats v):
  //   0 3aaffd01 201
endmodule
