// Logisim project subtraction using 2s compliment 8BIT.circ as structural Verilog: 1 circuit, main circuit main
module main (
  input  in_1,
  input  in_2,
  input  in_3,
  input  in_4,
  input  in_5,
  input  in_6,
  input  in_7,
  input  in_8,
  input  in_9,
  input  in_10,
  input  in_11,
  input  in_12,
  input  in_13,
  input  in_14,
  input  in_15,
  input  in_16,
  output out_17,
  output out_18,
  output out_19,
  output out_20,
  output out_21,
  output out_22,
  output out_23,
  output out_24
);

  wire and_1_out, and_2_out, and_3_out, and_4_out, and_5_out, and_6_out, and_7_out, and_8_out, and_9_out,
       and_10_out, and_11_out, and_12_out, and_13_out, and_14_out, and_15_out, and_16_out, and_17_out,
       and_18_out, and_19_out, and_20_out, and_21_out, and_22_out, and_23_out, and_24_out, not_1_out,
       not_2_out, not_3_out, not_4_out, not_5_out, not_6_out, not_7_out, not_8_out, or_1_out, or_2_out,
       or_3_out, or_4_out, or_5_out, or_6_out, or_7_out, or_8_out, xor_1_out, xor_2_out, xor_3_out,
       xor_4_out, xor_5_out, xor_6_out, xor_7_out, xor_8_out, xor_9_out, xor_10_out, xor_11_out, xor_12_out,
       xor_13_out, xor_14_out, xor_15_out, xor_16_out;

  not not_1 (not_1_out, in_9);
  not not_2 (not_2_out, in_12);
  not not_3 (not_3_out, in_11);
  not not_4 (not_4_out, in_10);
  not not_5 (not_5_out, in_15);
  not not_6 (not_6_out, in_14);
  not not_7 (not_7_out, in_13);
  not not_8 (not_8_out, in_16);
  xor xor_1 (xor_1_out, 1'b1, not_8_out);
  and and_1 (and_1_out, 1'b1, not_8_out);
  xor xor_2 (xor_2_out, and_1_out, not_5_out);
  and and_2 (and_2_out, and_1_out, not_5_out);
  xor xor_3 (xor_3_out, and_2_out, not_6_out);
  and and_3 (and_3_out, and_2_out, not_6_out);
  xor xor_4 (xor_4_out, and_3_out, not_7_out);
  and and_4 (and_4_out, and_3_out, not_7_out);
  xor xor_5 (xor_5_out, and_4_out, not_2_out);
  and and_5 (and_5_out, and_4_out, not_2_out);
  xor xor_6 (xor_6_out, and_5_out, not_3_out);
  and and_6 (and_6_out, and_5_out, not_3_out);
  xor xor_7 (xor_7_out, and_6_out, not_4_out);
  and and_7 (and_7_out, and_6_out, not_4_out);
  xor xor_8 (xor_8_out, and_7_out, not_1_out);
  and and_8 (and_8_out, and_7_out, not_1_out);
  xor xor_9 (xor_9_out, xor_1_out, in_8);
  and and_9 (and_9_out, xor_1_out, in_8);
  xor xor_10 (xor_10_out, xor_2_out, in_7);
  and and_10 (and_10_out, xor_2_out, in_7);
  xor xor_11 (xor_11_out, xor_3_out, in_6);
  and and_11 (and_11_out, xor_3_out, in_6);
  xor xor_12 (xor_12_out, xor_4_out, in_5);
  and and_12 (and_12_out, xor_4_out, in_5);
  xor xor_13 (xor_13_out, xor_5_out, in_4);
  and and_13 (and_13_out, xor_5_out, in_4);
  xor xor_14 (xor_14_out, xor_6_out, in_3);
  and and_14 (and_14_out, xor_6_out, in_3);
  xor xor_15 (xor_15_out, xor_7_out, in_2);
  and and_15 (and_15_out, xor_7_out, in_2);
  xor xor_16 (xor_16_out, xor_8_out, in_1);
  and and_16 (and_16_out, xor_8_out, in_1);
  xor xor_17 (out_24, 1'b0, xor_9_out);
  and and_17 (and_17_out, 1'b0, xor_9_out);
  xor xor_18 (out_23, or_1_out, xor_10_out);
  and and_18 (and_18_out, or_1_out, xor_10_out);
  xor xor_19 (out_22, or_2_out, xor_11_out);
  and and_19 (and_19_out, or_2_out, xor_11_out);
  xor xor_20 (out_21, or_3_out, xor_12_out);
  and and_20 (and_20_out, or_3_out, xor_12_out);
  xor xor_21 (out_20, or_4_out, xor_13_out);
  and and_21 (and_21_out, or_4_out, xor_13_out);
  xor xor_22 (out_19, or_5_out, xor_14_out);
  and and_22 (and_22_out, or_5_out, xor_14_out);
  xor xor_23 (out_18, or_6_out, xor_15_out);
  and and_23 (and_23_out, or_6_out, xor_15_out);
  xor xor_24 (out_17, or_7_out, xor_16_out);
  and and_24 (and_24_out, or_7_out, xor_16_out);
  or or_1 (or_1_out, and_17_out, and_9_out);
  or or_2 (or_2_out, and_18_out, and_10_out);
  or or_3 (or_3_out, and_19_out, and_11_out);
  or or_4 (or_4_out, and_20_out, and_12_out);
  or or_5 (or_5_out, and_21_out, and_13_out);
  or or_6 (or_6_out, and_22_out, and_14_out);
  or or_7 (or_7_out, and_23_out, and_15_out);
  or or_8 (or_8_out, and_24_out, and_16_out);
endmodule
